# Fritzing sketch Sketch Omnitrix (saved by Fritzing 0.9.3b)
circuit board: 5cm x 5cm
breadboards: 1

parts:
  RE1 = KY-040 Rotary encoder [package=THT]
  R1 = Resistor [tolerance=±5% resistance=10k package=THT]
  BTN = Pushbutton [package="[THT]"]
  LCD1 = Waveshare 1.28 inch Round 240x240 LCD Display
  BOARD = Wemos S2 Mini [part_number="WeMos D1 Mini Lite"]

nets:
  N1: RE1.GND, R1.Pin_1, LCD1.pin2, BOARD.Pin_17, BOARD.Pin_18
  N2: RE1.Vcc, BTN.Pin_3, BTN.Pin_4, LCD1.pin_1, BOARD.Pin_8
  N3: RE1.SW, R1.Pin_0, BTN.Pin_1, BTN.Pin_2, BOARD.Pin_4, BOARD.Pin_22
  N4: RE1.DT, BOARD.Pin_21, BOARD.Pin_32
  N5: RE1.CLK, BOARD.Pin_20, BOARD.Pin_24
  N6: LCD1.pin3, BOARD.Pin_31
  N7: LCD1.pin4, BOARD.Pin_30
  N8: LCD1.pin_5, BOARD.Pin_14
  N9: LCD1.pin_6, BOARD.Pin_13
  N10: LCD1.pin_7, BOARD.Pin_12

custom parts:
  KY-040 Rotary encoder: KY-040 Rotary Encoder with switch on breakout borad from AZ Delivery
  Waveshare 1.28 inch Round 240x240 LCD Display: Waveshare 1.28 inch Round 240x240 LCD Display with GC9A01 Controller
  Wemos S2 Mini: A mini wifi board based on the ESP32-S2FN4R2.
